# Fritzing sketch led2 (saved by Fritzing 0.8.7b)
breadboards: 1

parts:
  LED1 = LED - 5mm [color="Red (633nm)" package="5 mm [THT]"]
  R1 = Resistor [tolerance=±5% resistance=330 package=THT]
  부품1 = Arduino Uno (Rev3)
  LED2 = LED - 5mm [color="Red (633nm)" package="5 mm [THT]"]
  R2 = Resistor [tolerance=±5% resistance=330 package=THT]

nets:
  N1: LED1.cathode, 부품1.GND, LED2.cathode
  N2: LED1.anode, R1.Pin_0
  N3: R1.Pin_1, 부품1.D8
  N4: 부품1.D6_PWM, R2.Pin_1
  N5: LED2.anode, R2.Pin_0
